# Fritzing sketch Breadboard (saved by Fritzing 0.9.3b)
breadboards: 1

parts:
  Grove1 = Grove 4 Digit Display
  R1 = Resistor [tolerance=±5% resistance=22k package=THT]
  R2 = Resistor [tolerance=±5% resistance=10k package=THT]
  R3 = Resistor [tolerance=±5% resistance=10k package=THT]
  U1 = NodeMCU V1.0
  S1 = Pushbutton [package="[THT]"]
  SG1 = Buzzer 12mm [package=buzzer-12mm-ns]
  U2 = mystery part, 3 pins [chip_label=LD33V]  # not connected

nets:
  N1: Grove1.GND, S1.Pin_1, S1.Pin_2, SG1.1
  N2: Grove1.CLK, U1.D0
  N3: R1.Pin_0, R2.Pin_1, U1.A0
  N4: R1.Pin_1, R3.Pin_0
  N5: U1.D2, S1.Pin_3, S1.Pin_4
  N6: U1.D3, U1.SD3, SG1.2

custom parts:
  NodeMCU V1.0: ESP8266 based NodeMCU
